// Logisim project Logisim_4BitSort.circ as structural Verilog
module _1bit_swap (
  input  in_1,
  input  in_2,
  input  in_3,
  output out_4,
  output out_5
);

  wire and_1_out, and_2_out, and_3_out, and_4_out, not_1_out;

  not not_1 (not_1_out, in_3);
  and and_1 (and_1_out, in_1, not_1_out);
  and and_2 (and_2_out, in_2, in_3);
  and and_3 (and_3_out, in_3, in_1);
  and and_4 (and_4_out, in_2, not_1_out);
  or or_1 (out_4, and_1_out, and_2_out);
  or or_2 (out_5, and_3_out, and_4_out);
endmodule

module _4bit_swap (
  input  [3:0] in_1,
  input  [3:0] in_2,
  output [3:0] out_3,
  output [3:0] out_4
);

  wire comparator_1_gt;

  Comparator #(.width(4), .mode("unsigned")) comparator_1 (.a(in_1), .b(in_2), .gt(comparator_1_gt));  // open: eq, lt
  _1bit_swap u_1bit_swap_1 (.in_1(in_1[0]), .in_2(in_2[0]), .in_3(comparator_1_gt), .out_4(out_3[0]), .out_5(out_4[0]));
  _1bit_swap u_1bit_swap_2 (.in_1(in_1[1]), .in_2(in_2[1]), .in_3(comparator_1_gt), .out_4(out_3[1]), .out_5(out_4[1]));
  _1bit_swap u_1bit_swap_3 (.in_1(in_1[2]), .in_2(in_2[2]), .in_3(comparator_1_gt), .out_4(out_3[2]), .out_5(out_4[2]));
  _1bit_swap u_1bit_swap_4 (.in_1(in_1[3]), .in_2(in_2[3]), .in_3(comparator_1_gt), .out_4(out_3[3]), .out_5(out_4[3]));
endmodule

module _4bit_sort (
  input  [3:0] A,
  input  [3:0] B,
  input  [3:0] C,
  input  [3:0] D,
  output [3:0] _1,
  output [3:0] _2,
  output [3:0] _3,
  output [3:0] _4
);

  wire [3:0] n4bit_swap_1_out_3, n4bit_swap_1_out_4, n4bit_swap_2_out_3, n4bit_swap_2_out_4,
       n4bit_swap_3_out_3, n4bit_swap_3_out_4, n4bit_swap_4_out_3, n4bit_swap_6_out_3;

  _4bit_swap u_4bit_swap_1 (.in_1(A), .in_2(B), .out_3(n4bit_swap_1_out_3), .out_4(n4bit_swap_1_out_4));
  _4bit_swap u_4bit_swap_2 (
    .in_1(n4bit_swap_1_out_4), .in_2(C), .out_3(n4bit_swap_2_out_3), .out_4(n4bit_swap_2_out_4));
  _4bit_swap u_4bit_swap_3 (
    .in_1(n4bit_swap_1_out_3), .in_2(n4bit_swap_2_out_3), .out_3(n4bit_swap_3_out_3),
    .out_4(n4bit_swap_3_out_4));
  _4bit_swap u_4bit_swap_4 (.in_1(n4bit_swap_2_out_4), .in_2(D), .out_3(n4bit_swap_4_out_3), .out_4(_4));
  _4bit_swap u_4bit_swap_5 (.in_1(n4bit_swap_3_out_3), .in_2(n4bit_swap_6_out_3), .out_3(_1), .out_4(_2));
  _4bit_swap u_4bit_swap_6 (
    .in_1(n4bit_swap_3_out_4), .in_2(n4bit_swap_4_out_3), .out_3(n4bit_swap_6_out_3), .out_4(_3));
endmodule
