// Logisim project Logisim_mod5.circ as structural Verilog
module mod5 (
  input  In,
  output s0,
  output s1,
  output s2,
  output s3,
  output s4
);

  wire clock_1_out, not_1_out;
  wire [1:0] multiplexer_1_out, register_1_q;

  not not_1 (not_1_out, In);
  Multiplexer #(.select(2), .width(2)) multiplexer_1 (
    .in0(2'b00), .in1(2'b10), .in2(2'b00), .in3(2'b10), .out(multiplexer_1_out), .sel(register_1_q),
    .en(not_1_out));
  Multiplexer #(.select(2), .width(2)) multiplexer_2 (
    .in0(2'b01), .in1(2'b11), .in2(2'b01), .in3(2'b11), .out(multiplexer_1_out), .sel(register_1_q), .en(In));
  Register #(.width(2)) register_1 (.D(multiplexer_1_out), .Q(register_1_q), .clk(clock_1_out));  // open: en, clr
  Clock clock_1 (.out(clock_1_out));
  Decoder #(.select(2)) decoder_1 (.out0(s1), .out1(s2), .out2(s4), .out3(s3), .sel(multiplexer_1_out));  // open: en

  assign s0 = 1'b0;
endmodule
