// Logisim project crc.circ as structural Verilog
module CRC (
  input  [7:0] A,
  input  [3:0] B,
  output [10:0] C
);

  wire [2:0] div_1_out_3, div_2_out_3, div_3_out_3, div_4_out_3, div_5_out_3, div_6_out_3, div_7_out_3;

  div div_1 (.in_1(A[7:4]), .in_2(B), .out_3(div_1_out_3));
  div div_2 (.in_1({div_1_out_3, A[3]}), .in_2(B), .out_3(div_2_out_3));
  div div_3 (.in_1({div_2_out_3, A[2]}), .in_2(B), .out_3(div_3_out_3));
  div div_4 (.in_1({div_3_out_3, A[1]}), .in_2(B), .out_3(div_4_out_3));
  div div_5 (.in_1({div_4_out_3, A[0]}), .in_2(B), .out_3(div_5_out_3));
  div div_6 (.in_1({div_5_out_3, 1'b0}), .in_2(B), .out_3(div_6_out_3));
  div div_7 (.in_1({div_6_out_3, 1'b0}), .in_2(B), .out_3(div_7_out_3));
  div div_8 (.in_1({div_7_out_3, 1'b0}), .in_2(B), .out_3(C[2:0]));

  assign C[10:3] = A;
endmodule

module div (
  input  [3:0] in_1,
  input  [3:0] in_2,
  output [2:0] out_3
);

  wire [2:0] xor_1_out;

  xor xor_1 (xor_1_out[0], in_1[0], in_2[0]);
  xor xor_2 (xor_1_out[1], in_1[1], in_2[1]);
  xor xor_3 (xor_1_out[2], in_1[2], in_2[2]);
  Multiplexer #(.width(3)) multiplexer_1 (.in0(in_1[2:0]), .in1(xor_1_out), .out(out_3), .sel(in_1[3]));  // open: en
endmodule
