// Logisim project fibonacci1.circ as structural Verilog: 1 circuit, main circuit main
module main (
  input  [2:0] in_1,
  output [3:0] out_2
);

  wire adder_1_cout, clock_1_out, comparator_1_eq, comparator_2_eq;
  wire [2:0] counter_1_q;
  wire [3:0] adder_1_out, register_1_q, register_2_q;

  Counter #(.width(3), .max('h7)) counter_1 (.Q(counter_1_q), .clk(clock_1_out));  // open: load, D, count, carry, clr
  Clock clock_1 (.out(clock_1_out));
  Comparator #(.width(3)) comparator_1 (.a(in_1), .b(counter_1_q), .eq(comparator_1_eq));  // open: gt, lt
  Register #(.width(4)) register_1 (
    .D(register_2_q), .Q(register_1_q), .clk(clock_1_out), .clr(adder_1_cout));  // open: en
  Register #(.width(4)) register_2 (
    .D(adder_1_out), .Q(register_2_q), .clk(clock_1_out), .clr(adder_1_cout));  // open: en
  Comparator #(.width(3)) comparator_2 (.a(3'b000), .b(counter_1_q), .eq(comparator_2_eq));  // open: gt, lt
  Adder #(.width(4)) adder_1 (
    .a(register_1_q), .b(register_2_q), .out(adder_1_out), .cin(comparator_2_eq), .cout(adder_1_cout));
  Register #(.width(4)) register_3 (.D(adder_1_out), .Q(out_2), .clk(comparator_1_eq));  // open: en, clr
endmodule
