// Logisim project fsm.circ as structural Verilog
module fsm (
  input  CLR,
  input  [1:0] In,
  output Z
);

  wire clock_1_out, decoder_1_out0, decoder_1_out1, decoder_1_out2, decoder_1_out3;
  wire [1:0] multiplexer_1_out, multiplexer_5_out, multiplexer_6_out, register_1_q;

  Decoder #(.select(2)) decoder_1 (
    .out0(decoder_1_out0), .out1(decoder_1_out1), .out2(decoder_1_out2), .out3(decoder_1_out3), .sel(In));  // open: en
  Multiplexer #(.select(2), .width(2)) multiplexer_1 (
    .in0(2'b00), .in1(2'b10), .in2(2'b11), .in3(2'b00), .out(multiplexer_1_out), .sel(register_1_q),
    .en(decoder_1_out0));
  Multiplexer #(.select(2), .width(2)) multiplexer_2 (
    .in0(2'b01), .in1(2'b01), .in2(2'b01), .in3(2'b01), .out(multiplexer_1_out), .sel(register_1_q),
    .en(decoder_1_out1));
  Multiplexer #(.select(2), .width(2)) multiplexer_3 (
    .in0(2'b00), .in1(2'b10), .in2(2'b11), .in3(2'b00), .out(multiplexer_1_out), .sel(register_1_q),
    .en(decoder_1_out2));
  Multiplexer #(.select(2), .width(2)) multiplexer_4 (
    .in0(2'b00), .in1(2'b00), .in2(2'b00), .in3(2'b00), .out(multiplexer_1_out), .sel(register_1_q),
    .en(decoder_1_out3));
  Clock clock_1 (.out(clock_1_out));
  Multiplexer #(.width(2)) multiplexer_5 (
    .in0(multiplexer_1_out), .in1(2'b00), .out(multiplexer_5_out), .sel(CLR));  // open: en
  Register #(.width(2)) register_1 (.D(multiplexer_5_out), .Q(register_1_q), .clk(clock_1_out));  // open: en, clr
  Multiplexer #(.select(2), .width(2)) multiplexer_6 (
    .in0(2'b00), .in1(2'b10), .in2(2'b11), .in3(2'b00), .out(multiplexer_6_out), .sel(register_1_q),
    .en(decoder_1_out0));
  Multiplexer #(.select(2), .width(2)) multiplexer_7 (
    .in0(2'b01), .in1(2'b01), .in2(2'b01), .in3(2'b01), .out(multiplexer_6_out), .sel(register_1_q),
    .en(decoder_1_out1));
  Multiplexer #(.select(2), .width(2)) multiplexer_8 (
    .in0(2'b00), .in1(2'b10), .in2(2'b11), .in3(2'b00), .out(multiplexer_6_out), .sel(register_1_q),
    .en(decoder_1_out2));
  Multiplexer #(.select(2), .width(2)) multiplexer_9 (
    .in0(2'b00), .in1(2'b00), .in2(2'b00), .in3(2'b00), .out(multiplexer_6_out), .sel(register_1_q),
    .en(decoder_1_out3));
  Decoder #(.select(2)) decoder_2 (.out3(Z), .sel(multiplexer_6_out));  // open: out0, out1, out2, en
endmodule
