// Logisim project ftoi.circ as structural Verilog
module ftoi (
  input  [15:0] float,
  output [31:0] \int 
);

  wire isonly0_1_out_2;
  wire [31:0] geti_1_out_2;

  geti geti_1 (.in_1(float), .out_2(geti_1_out_2));
  isonly0 isonly0_1 (.in_1(float), .out_2(isonly0_1_out_2));
  Multiplexer #(.width(32)) multiplexer_1 (
    .in0(geti_1_out_2), .in1({32{1'b0}}), .out(\int ), .sel(isonly0_1_out_2));  // open: en
endmodule

module isonly0 (
  input  [15:0] in_1,
  output out_2
);

  wire and_1_out, not_1_out, not_2_out, or_1_out;

  and and_1 (and_1_out, in_1[10], in_1[11], in_1[12], in_1[13], in_1[14]);
  or or_1 (or_1_out, in_1[10], in_1[11], in_1[12], in_1[13], in_1[14]);
  not not_1 (not_1_out, and_1_out);
  // AND_Gate and_2 has open pins: in0=or_1_out, in1=not_1_out, out=open
  not not_2 (not_2_out, or_1_out);
  or or_2 (out_2, not_2_out, and_1_out);
endmodule

module geti (
  input  [15:0] in_1,
  output [31:0] out_2
);

  wire comparator_1_eq, comparator_1_gt, comparator_1_lt;
  wire [4:0] subtractor_1_out;
  wire [31:0] negator_1_out, shifter_1_out, shifter_2_out;

  Comparator #(.width(5), .mode("unsigned")) comparator_1 (
    .a(in_1[14:10]), .b(5'b01111), .gt(comparator_1_gt), .eq(comparator_1_eq), .lt(comparator_1_lt));
  Shifter #(.width(32)) shifter_1 (.in({22'h1, in_1[9:0]}), .\dist (subtractor_1_out), .out(shifter_1_out));
  Subtractor #(.width(5)) subtractor_1 (.a(in_1[14:10]), .b(5'b01111), .out(subtractor_1_out));  // open: bin, bout
  Shifter #(.width(32), .shift("lr")) shifter_2 (.in(shifter_1_out), .\dist (5'b01010), .out(shifter_2_out));
  Negator #(.width(32)) negator_1 (.in(shifter_2_out), .out(negator_1_out));
  Multiplexer #(.width(32)) multiplexer_1 (
    .in0(shifter_2_out), .in1(negator_1_out), .out(out_2), .sel(in_1[15]), .en(comparator_1_gt));
  Multiplexer #(.width(32)) multiplexer_2 (
    .in0(32'h1), .in1({32{1'b1}}), .out(out_2), .sel(in_1[15]), .en(comparator_1_eq));
  Multiplexer #(.width(32)) multiplexer_3 (
    .in0({32{1'b0}}), .out(out_2), .sel(1'b0), .en(comparator_1_lt));  // open: in1
endmodule
