// Logisim project grf.circ as structural Verilog
module grf (
  input  clk,
  input  reset,
  input  WE,
  input  [4:0] A1,
  input  [4:0] A2,
  input  [4:0] A3,
  input  [31:0] WD,
  output [31:0] RD1,
  output [31:0] RD2
);

  wire demultiplexer_1_out0, demultiplexer_1_out1, demultiplexer_1_out2, demultiplexer_1_out3,
       demultiplexer_1_out4, demultiplexer_1_out5, demultiplexer_1_out6, demultiplexer_1_out7,
       demultiplexer_1_out8, demultiplexer_1_out9, demultiplexer_1_out10, demultiplexer_1_out11,
       demultiplexer_1_out12, demultiplexer_1_out13, demultiplexer_1_out14, demultiplexer_1_out15,
       demultiplexer_1_out16, demultiplexer_1_out17, demultiplexer_1_out18, demultiplexer_1_out19,
       demultiplexer_1_out20, demultiplexer_1_out21, demultiplexer_1_out22, demultiplexer_1_out23,
       demultiplexer_1_out24, demultiplexer_1_out25, demultiplexer_1_out26, demultiplexer_1_out27,
       demultiplexer_1_out28, demultiplexer_1_out29, demultiplexer_1_out30, demultiplexer_1_out31;
  wire [31:0] _0_q, _1_q, _2_q, _3_q, _4_q, _5_q, _6_q, _7_q, _8_q, _9_q, _10_q, _11_q, _12_q, _13_q, _14_q,
       _15_q, _16_q, _17_q, _18_q, _19_q, _20_q, _21_q, _22_q, _23_q, _24_q, _25_q, _26_q, _27_q, _28_q,
       _29_q, _30_q, _31_q;

  Demultiplexer #(.select(5)) demultiplexer_1 (
    .out0(demultiplexer_1_out0), .out1(demultiplexer_1_out1), .out2(demultiplexer_1_out2),
    .out3(demultiplexer_1_out3), .out4(demultiplexer_1_out4), .out5(demultiplexer_1_out5),
    .out6(demultiplexer_1_out6), .out7(demultiplexer_1_out7), .out8(demultiplexer_1_out8),
    .out9(demultiplexer_1_out9), .out10(demultiplexer_1_out10), .out11(demultiplexer_1_out11),
    .out12(demultiplexer_1_out12), .out13(demultiplexer_1_out13), .out14(demultiplexer_1_out14),
    .out15(demultiplexer_1_out15), .out16(demultiplexer_1_out16), .out17(demultiplexer_1_out17),
    .out18(demultiplexer_1_out18), .out19(demultiplexer_1_out19), .out20(demultiplexer_1_out20),
    .out21(demultiplexer_1_out21), .out22(demultiplexer_1_out22), .out23(demultiplexer_1_out23),
    .out24(demultiplexer_1_out24), .out25(demultiplexer_1_out25), .out26(demultiplexer_1_out26),
    .out27(demultiplexer_1_out27), .out28(demultiplexer_1_out28), .out29(demultiplexer_1_out29),
    .out30(demultiplexer_1_out30), .out31(demultiplexer_1_out31), .in(WE), .sel(A3));  // open: en
  Register #(.width(32)) _0 (.en(demultiplexer_1_out0), .Q(_0_q), .clk(clk), .clr(reset));  // open: D
  Register #(.width(32)) _1 (.D(WD), .en(demultiplexer_1_out1), .Q(_1_q), .clk(clk), .clr(reset));
  Register #(.width(32)) _2 (.D(WD), .en(demultiplexer_1_out2), .Q(_2_q), .clk(clk), .clr(reset));
  Register #(.width(32)) _3 (.D(WD), .en(demultiplexer_1_out3), .Q(_3_q), .clk(clk), .clr(reset));
  Register #(.width(32)) _4 (.D(WD), .en(demultiplexer_1_out4), .Q(_4_q), .clk(clk), .clr(reset));
  Register #(.width(32)) _5 (.D(WD), .en(demultiplexer_1_out5), .Q(_5_q), .clk(clk), .clr(reset));
  Register #(.width(32)) _6 (.D(WD), .en(demultiplexer_1_out6), .Q(_6_q), .clk(clk), .clr(reset));
  Register #(.width(32)) _7 (.D(WD), .en(demultiplexer_1_out7), .Q(_7_q), .clk(clk), .clr(reset));
  Register #(.width(32)) _8 (.D(WD), .en(demultiplexer_1_out8), .Q(_8_q), .clk(clk), .clr(reset));
  Register #(.width(32)) _9 (.D(WD), .en(demultiplexer_1_out9), .Q(_9_q), .clk(clk), .clr(reset));
  Register #(.width(32)) _10 (.D(WD), .en(demultiplexer_1_out10), .Q(_10_q), .clk(clk), .clr(reset));
  Register #(.width(32)) _11 (.D(WD), .en(demultiplexer_1_out11), .Q(_11_q), .clk(clk), .clr(reset));
  Register #(.width(32)) _12 (.D(WD), .en(demultiplexer_1_out12), .Q(_12_q), .clk(clk), .clr(reset));
  Register #(.width(32)) _13 (.D(WD), .en(demultiplexer_1_out13), .Q(_13_q), .clk(clk), .clr(reset));
  Register #(.width(32)) _14 (.D(WD), .en(demultiplexer_1_out14), .Q(_14_q), .clk(clk), .clr(reset));
  Register #(.width(32)) _15 (.D(WD), .en(demultiplexer_1_out15), .Q(_15_q), .clk(clk), .clr(reset));
  Register #(.width(32)) _16 (.D(WD), .en(demultiplexer_1_out16), .Q(_16_q), .clk(clk), .clr(reset));
  Register #(.width(32)) _17 (.D(WD), .en(demultiplexer_1_out17), .Q(_17_q), .clk(clk), .clr(reset));
  Register #(.width(32)) _18 (.D(WD), .en(demultiplexer_1_out18), .Q(_18_q), .clk(clk), .clr(reset));
  Register #(.width(32)) _19 (.D(WD), .en(demultiplexer_1_out19), .Q(_19_q), .clk(clk), .clr(reset));
  Register #(.width(32)) _20 (.D(WD), .en(demultiplexer_1_out20), .Q(_20_q), .clk(clk), .clr(reset));
  Register #(.width(32)) _21 (.D(WD), .en(demultiplexer_1_out21), .Q(_21_q), .clk(clk), .clr(reset));
  Register #(.width(32)) _22 (.D(WD), .en(demultiplexer_1_out22), .Q(_22_q), .clk(clk), .clr(reset));
  Register #(.width(32)) _23 (.D(WD), .en(demultiplexer_1_out23), .Q(_23_q), .clk(clk), .clr(reset));
  Register #(.width(32)) _24 (.D(WD), .en(demultiplexer_1_out24), .Q(_24_q), .clk(clk), .clr(reset));
  Register #(.width(32)) _25 (.D(WD), .en(demultiplexer_1_out25), .Q(_25_q), .clk(clk), .clr(reset));
  Register #(.width(32)) _26 (.D(WD), .en(demultiplexer_1_out26), .Q(_26_q), .clk(clk), .clr(reset));
  Register #(.width(32)) _27 (.D(WD), .en(demultiplexer_1_out27), .Q(_27_q), .clk(clk), .clr(reset));
  Register #(.width(32)) _28 (.D(WD), .en(demultiplexer_1_out28), .Q(_28_q), .clk(clk), .clr(reset));
  Register #(.width(32)) _29 (.D(WD), .en(demultiplexer_1_out29), .Q(_29_q), .clk(clk), .clr(reset));
  Register #(.width(32)) _30 (.D(WD), .en(demultiplexer_1_out30), .Q(_30_q), .clk(clk), .clr(reset));
  Register #(.width(32)) _31 (.D(WD), .en(demultiplexer_1_out31), .Q(_31_q), .clk(clk), .clr(reset));
  Multiplexer #(.select(5), .width(32)) multiplexer_1 (
    .in0(_0_q), .in1(_1_q), .in2(_2_q), .in3(_3_q), .in4(_4_q), .in5(_5_q), .in6(_6_q), .in7(_7_q),
    .in8(_8_q), .in9(_9_q), .in10(_10_q), .in11(_11_q), .in12(_12_q), .in13(_13_q), .in14(_14_q),
    .in15(_15_q), .in16(_16_q), .in17(_17_q), .in18(_18_q), .in19(_19_q), .in20(_20_q), .in21(_21_q),
    .in22(_22_q), .in23(_23_q), .in24(_24_q), .in25(_25_q), .in26(_26_q), .in27(_27_q), .in28(_28_q),
    .in29(_29_q), .in30(_30_q), .in31(_31_q), .out(RD2), .sel(A2));  // open: en
  Multiplexer #(.select(5), .width(32)) multiplexer_2 (
    .in0(_0_q), .in1(_1_q), .in2(_2_q), .in3(_3_q), .in4(_4_q), .in5(_5_q), .in6(_6_q), .in7(_7_q),
    .in8(_8_q), .in9(_9_q), .in10(_10_q), .in11(_11_q), .in12(_12_q), .in13(_13_q), .in14(_14_q),
    .in15(_15_q), .in16(_16_q), .in17(_17_q), .in18(_18_q), .in19(_19_q), .in20(_20_q), .in21(_21_q),
    .in22(_22_q), .in23(_23_q), .in24(_24_q), .in25(_25_q), .in26(_26_q), .in27(_27_q), .in28(_28_q),
    .in29(_29_q), .in30(_30_q), .in31(_31_q), .out(RD1), .sel(A1));  // open: en
endmodule
