// Logisim project navigator.circ as structural Verilog
module navigation (
  input  [1:0] dir,
  input  clk,
  input  reset,
  output arrive,
  output hit
);

  wire clock_1_out, isinvalid_1_out_3, multiplexer_5_out;
  wire [1:0] command_1_nextx, command_1_nexty, multiplexer_1_out, multiplexer_2_out, multiplexer_3_out,
       multiplexer_4_out, x_q, y_q;

  Clock clock_1 (.out(clock_1_out));
  command command_1 (.lastX(x_q), .lastY(y_q), .nav(dir), .nextX(command_1_nextx), .nextY(command_1_nexty));
  Multiplexer #(.width(2)) multiplexer_1 (
    .in0(command_1_nextx), .in1(x_q), .out(multiplexer_1_out), .sel(isinvalid_1_out_3));  // open: en
  Multiplexer #(.width(2)) multiplexer_2 (
    .in0(command_1_nexty), .in1(y_q), .out(multiplexer_2_out), .sel(isinvalid_1_out_3));  // open: en
  Multiplexer #(.width(2)) multiplexer_3 (
    .in0(multiplexer_1_out), .in1(2'b00), .out(multiplexer_3_out), .sel(arrive));  // open: en
  Multiplexer #(.width(2)) multiplexer_4 (
    .in0(multiplexer_2_out), .in1(2'b00), .out(multiplexer_4_out), .sel(arrive));  // open: en
  Register #(.width(2)) x (.D(multiplexer_3_out), .Q(x_q), .clk(clock_1_out), .clr(reset));  // open: en
  Register #(.width(2)) y (.D(multiplexer_4_out), .Q(y_q), .clk(clock_1_out), .clr(reset));  // open: en
  isInvalid isinvalid_1 (.in_1(command_1_nextx), .in_2(command_1_nexty), .out_3(isinvalid_1_out_3));
  isArrived isarrived_1 (.x(x_q), .y(y_q), .out_3(arrive));
  Multiplexer multiplexer_5 (.in0(isinvalid_1_out_3), .in1(1'b0), .out(multiplexer_5_out), .sel(arrive));  // open: en
  Register #(.width(1)) register_1 (.D(multiplexer_5_out), .Q(hit), .clk(clock_1_out), .clr(reset));  // open: en
  Register #(.width(1)) register_2 ();  // open: D, en, Q, clk, clr
endmodule

module command (
  input  [1:0] lastX,
  input  [1:0] lastY,
  input  [1:0] nav,
  output [1:0] nextX,
  output [1:0] nextY
);

  wire [1:0] adder_1_out, adder_2_out, subtractor_1_out, subtractor_2_out;

  Adder #(.width(2)) adder_1 (.a(lastX), .b(2'b01), .out(adder_1_out));  // open: cin, cout
  Subtractor #(.width(2)) subtractor_1 (.a(lastX), .b(2'b01), .out(subtractor_1_out));  // open: bin, bout
  Adder #(.width(2)) adder_2 (.a(lastY), .b(2'b01), .out(adder_2_out));  // open: cin, cout
  Subtractor #(.width(2)) subtractor_2 (.a(lastY), .b(2'b01), .out(subtractor_2_out));  // open: bin, bout
  Multiplexer #(.select(2), .width(2)) multiplexer_1 (
    .in0(lastX), .in1(adder_1_out), .in2(lastX), .in3(subtractor_1_out), .out(nextX), .sel(nav));  // open: en
  Multiplexer #(.select(2), .width(2)) multiplexer_2 (
    .in0(adder_2_out), .in1(lastY), .in2(subtractor_2_out), .in3(lastY), .out(nextY), .sel(nav));  // open: en
endmodule

module isInvalid (
  input  [1:0] in_1,
  input  [1:0] in_2,
  output out_3
);

  wire and_1_out, comparator_1_eq, comparator_2_eq, comparator_3_gt, comparator_4_gt;

  Comparator #(.width(2), .mode("unsigned")) comparator_1 (.a(in_1), .b(2'b01), .eq(comparator_1_eq));  // open: gt, lt
  Comparator #(.width(2), .mode("unsigned")) comparator_2 (.a(in_2), .b(2'b00), .eq(comparator_2_eq));  // open: gt, lt
  and and_1 (and_1_out, comparator_2_eq, comparator_1_eq);
  Comparator #(.width(2), .mode("unsigned")) comparator_3 (.a(in_1), .b(2'b01), .gt(comparator_3_gt));  // open: eq, lt
  Comparator #(.width(2), .mode("unsigned")) comparator_4 (.a(in_2), .b(2'b10), .gt(comparator_4_gt));  // open: eq, lt
  or or_1 (out_3, comparator_4_gt, comparator_3_gt, and_1_out);
endmodule

module isArrived (
  input  [1:0] x,
  input  [1:0] y,
  output out_3
);

  wire comparator_1_eq, comparator_2_eq;

  Comparator #(.width(2), .mode("unsigned")) comparator_1 (.a(x), .b(2'b01), .eq(comparator_1_eq));  // open: gt, lt
  Comparator #(.width(2), .mode("unsigned")) comparator_2 (.a(y), .b(2'b10), .eq(comparator_2_eq));  // open: gt, lt
  and and_1 (out_3, comparator_1_eq, comparator_2_eq);
endmodule
