// Logisim project sokoban.circ as structural Verilog
module Sokoban (
  input  dx,
  input  dy,
  input  clk,
  input  reset,
  output out,
  output flag
);

  wire isinvalid_1_out_3;
  wire [2:0] adder_1_out, adder_2_out, bit_extender_1_out, bit_extender_2_out, multiplexer_1_out,
       multiplexer_2_out, register_2_q, register_3_q;

  Clock clock_1 ();  // open: out
  assign bit_extender_1_out = {{2{1'b0}}, dx};  // Bit_Extender bit_extender_1
  assign bit_extender_2_out = {{2{1'b0}}, dy};  // Bit_Extender bit_extender_2
  Adder #(.width(3)) adder_1 (.a(register_2_q), .b(bit_extender_1_out), .out(adder_1_out));  // open: cin, cout
  Adder #(.width(3)) adder_2 (.a(register_3_q), .b(bit_extender_2_out), .out(adder_2_out));  // open: cin, cout
  Multiplexer #(.width(3)) multiplexer_1 (
    .in0(adder_1_out), .in1(register_2_q), .out(multiplexer_1_out), .sel(isinvalid_1_out_3));  // open: en
  Multiplexer #(.width(3)) multiplexer_2 (
    .in0(adder_2_out), .in1(register_3_q), .out(multiplexer_2_out), .sel(isinvalid_1_out_3));  // open: en
  isInvalid isinvalid_1 (.x(adder_1_out), .y(adder_2_out), .out_3(isinvalid_1_out_3));
  Register #(.width(1)) register_1 (.D(isinvalid_1_out_3), .Q(flag), .clk(clk), .clr(reset));  // open: en
  Register #(.width(3)) register_2 (.D(multiplexer_1_out), .Q(register_2_q), .clk(clk), .clr(reset));  // open: en
  Register #(.width(3)) register_3 (.D(multiplexer_2_out), .Q(register_3_q), .clk(clk), .clr(reset));  // open: en
  isArrived isarrived_1 (.x(register_2_q), .y(register_3_q), .out_3(out));
endmodule

module isInvalid (
  input  [2:0] x,
  input  [2:0] y,
  output out_3
);

  wire and_1_out, and_2_out, and_3_out, and_4_out, and_5_out, and_6_out, comparator_1_eq, comparator_2_eq,
       comparator_3_eq, comparator_4_eq, comparator_5_eq, comparator_6_eq, comparator_7_eq, comparator_8_eq,
       comparator_9_eq, comparator_10_eq, comparator_11_eq, comparator_12_eq, comparator_13_gt,
       comparator_14_gt, or_1_out, or_3_out;

  Comparator #(.width(3), .mode("unsigned")) comparator_1 (.a(x), .b(3'b001), .eq(comparator_1_eq));  // open: gt, lt
  Comparator #(.width(3), .mode("unsigned")) comparator_2 (.a(y), .b(3'b001), .eq(comparator_2_eq));  // open: gt, lt
  and and_1 (and_1_out, comparator_2_eq, comparator_1_eq);
  Comparator #(.width(3), .mode("unsigned")) comparator_3 (.a(x), .b(3'b010), .eq(comparator_3_eq));  // open: gt, lt
  Comparator #(.width(3), .mode("unsigned")) comparator_4 (.a(y), .b(3'b001), .eq(comparator_4_eq));  // open: gt, lt
  and and_2 (and_2_out, comparator_4_eq, comparator_3_eq);
  Comparator #(.width(3), .mode("unsigned")) comparator_5 (.a(x), .b(3'b001), .eq(comparator_5_eq));  // open: gt, lt
  Comparator #(.width(3), .mode("unsigned")) comparator_6 (.a(y), .b(3'b010), .eq(comparator_6_eq));  // open: gt, lt
  and and_3 (and_3_out, comparator_6_eq, comparator_5_eq);
  or or_1 (or_1_out, and_1_out, and_2_out, and_3_out, and_4_out, and_5_out, and_6_out);
  Comparator #(.width(3), .mode("unsigned")) comparator_7 (.a(x), .b(3'b100), .eq(comparator_7_eq));  // open: gt, lt
  Comparator #(.width(3), .mode("unsigned")) comparator_8 (.a(y), .b(3'b100), .eq(comparator_8_eq));  // open: gt, lt
  and and_4 (and_4_out, comparator_8_eq, comparator_7_eq);
  Comparator #(.width(3), .mode("unsigned")) comparator_9 (.a(x), .b(3'b011), .eq(comparator_9_eq));  // open: gt, lt
  Comparator #(.width(3), .mode("unsigned")) comparator_10 (.a(y), .b(3'b100), .eq(comparator_10_eq));  // open: gt, lt
  and and_5 (and_5_out, comparator_10_eq, comparator_9_eq);
  or or_2 (out_3, or_3_out, or_1_out);
  Comparator #(.width(3), .mode("unsigned")) comparator_11 (.a(x), .b(3'b100), .eq(comparator_11_eq));  // open: gt, lt
  Comparator #(.width(3), .mode("unsigned")) comparator_12 (.a(y), .b(3'b011), .eq(comparator_12_eq));  // open: gt, lt
  and and_6 (and_6_out, comparator_12_eq, comparator_11_eq);
  Comparator #(.width(3), .mode("unsigned")) comparator_13 (.a(y), .b(3'b101), .gt(comparator_13_gt));  // open: eq, lt
  Comparator #(.width(3), .mode("unsigned")) comparator_14 (.a(x), .b(3'b101), .gt(comparator_14_gt));  // open: eq, lt
  or or_3 (or_3_out, comparator_13_gt, comparator_14_gt);
endmodule

module isArrived (
  input  [2:0] x,
  input  [2:0] y,
  output out_3
);

  wire comparator_1_eq, comparator_2_eq;

  Comparator #(.width(3), .mode("unsigned")) comparator_1 (.a(x), .b(3'b101), .eq(comparator_1_eq));  // open: gt, lt
  Comparator #(.width(3), .mode("unsigned")) comparator_2 (.a(3'b101), .b(y), .eq(comparator_2_eq));  // open: gt, lt
  and and_1 (out_3, comparator_1_eq, comparator_2_eq);
endmodule
